# Fritzing sketch diagram (saved by Fritzing 0.9.3b)

parts:
  Part1 = Adafruit Metro M0 Express
  LED1 = RGB LED (com. cathode, rbg) [package="5 mm [THT]"]
  R1 = Rotary Potentiometer (Small) [maximum_resistance=100kΩ package=THT]
  U1 = SWITCH_SPDT [package=kps-1290]  # not connected
  R2 = Resistor [tolerance=±5% resistance=220 package=THT]
  Part2 = Adafruit TCS34725 RGB Color Sensor [part_number="Adafruit #1334"]
  Part3 = MQ-9 breakout
  R3 = Rotary Potentiometer (Small) [maximum_resistance=100kΩ package=THT]
  R4 = Rotary Potentiometer (Small) [maximum_resistance=100kΩ package=THT]
  R5 = Rotary Potentiometer (Small) [maximum_resistance=100kΩ package=THT]
  S2 = Round Pushbutton
  LED2 = smd LED [color="Red (633nm)" package="1206 [SMD]"]  # not connected
  J5 = Basic Servo
  J6 = Basic Servo
  J7 = Basic Servo
  J8 = Basic Servo
  R7 = Resistor [tolerance=±5% resistance=220 package=THT]
  R8 = Resistor [tolerance=±5% resistance=220 package=THT]
  U2 = SWITCH_SPDT [package=kps-1290]
  VCC4 = Battery
  VCC5 = Battery
  VCC6 = Battery
  J10 = female pin header, 5 pins [form="♀ (female)"]
  J11 = female pin header, 10 pins [form="♀ (female)"]
  J9 = double row female pin header, 20 pins [form="♀ (female)"]

nets:
  N1: Part1.A2, R4.wiper
  N2: Part1.A3, R1.wiper
  N3: Part1.A4, R5.wiper
  N4: Part1.A5, R3.wiper
  N5: Part1.SCL, Part2.SCL
  N6: Part1.SDA, Part2.SDA
  N7: Part1.D13, R2.Pin_0
  N8: Part1.D12, R8.Pin_0
  N9: Part1.D11, R7.Pin_0
  N10: Part1.D10, J5.pulse
  N11: Part1.D9, J6.pulse
  N12: Part1.D8, J7.pulse
  N13: Part1.D5, J8.pulse
  N14: Part1.D4, U2.P
  N15: Part1.D3, Part3.AO
  N16: Part1.D2, S2.leg0
  N17: Part1.+5V, J11.pin1
  N18: Part1.GND, J9.pin7
  N19: LED1.red_anode, R2.Pin_1
  N20: LED1.common_cathode, R8.Pin_1
  N21: LED1.blue_anode, J9.pin9
  N22: LED1.green_anode, R7.Pin_1
  N23: R1.leg1, J9.pin19
  N24: R1.leg2, J11.pin8
  N25: Part2.VIN, J11.pin3
  N26: Part2.GND, J9.pin5
  N27: Part3.VCC, J11.pin5
  N28: Part3.GND, J9.pin11
  N29: R3.leg1, J9.pin17
  N30: R3.leg2, J11.pin10
  N31: R4.leg1, J9.pin20
  N32: R4.leg2, J11.pin7
  N33: R5.leg1, J9.pin18
  N34: R5.leg2, J11.pin9
  N35: S2.leg1, J9.pin16
  N36: J5.gnd, J9.pin4
  N37: J5.vcc, J10.pin1
  N38: J6.gnd, J9.pin3
  N39: J6.vcc, J10.pin2
  N40: J7.gnd, J9.pin1
  N41: J7.vcc, J10.pin3
  N42: J8.gnd, J9.pin2
  N43: J8.vcc, J10.pin4
  N44: U2.O, J9.pin15
  N45: U2.S, J11.pin6
  N46: VCC4.-, VCC6.+
  N47: VCC4.+, VCC5.-

custom parts:
  Adafruit Metro M0 Express: Metro is our series of microcontroller boards for use with the Arduino IDE. This new Metro board looks a whole lot like our original Metro 328, but with a huge upgrade. Instead of the ATmega328, this Metro features a ATSAMD21G18 chip, an ARM Cortex M0+. It's our first Metro that is designed for use with CircuitPython! CircuitPython is our beginner-oriented flavor of MicroPython - and as the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
  Adafruit TCS34725 RGB Color Sensor: Your electronics can now see in dazzling color with this lovely color light sensor. We found the best color sensor on the market, the TCS34725, which has RGB and Clear light sensing elements. An IR blocking filter, integrated on-chip and localized to the color sensing photodiodes, minimizes the IR spectral component of the incoming light and allows color measurements to be made accurately. The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
  MQ-9 breakout: SKU: 101284
